# Fritzing sketch NoiseMeterL (saved by Fritzing 0.9.1b)

parts:
  Bauteil1 = Arduino Uno (Rev3)
  Bauteil2 = Breakout Board for Electret Microphone
  LED1 = LED_RING [package=led_ring]
  J1 = Piezo Speaker

nets:
  N1: Bauteil1.A0, Bauteil2.AUD
  N2: Bauteil1.D9_PWM, LED1.7
  N3: Bauteil1.D11_PWM/MOSI, J1.pin2
  GND: Bauteil1.GND, Bauteil2.GND, LED1.4, J1.pin1
  3V3: Bauteil1.AREF, Bauteil1.3V3, Bauteil2.VCC, LED1.6
