# Fritzing sketch ampel (saved by Fritzing 0.9.1b)
breadboards: 1

parts:
  Bauteil1 = Arduino Uno (Rev3)
  R1 = Resistor [tolerance=±5% resistance=220 package=THT]
  R2 = Resistor [tolerance=±5% resistance=220 package=THT]
  R3 = Resistor [tolerance=±5% resistance=220 package=THT]
  LED1 = LED - 5mm [color="Red (633nm)" package="5 mm [THT]"]
  LED2 = LED - 5mm [color="Yellow (595nm)" package="5 mm [THT]"]
  LED3 = LED - 5mm [color="Green (565nm)" package="5 mm [THT]"]
  R4 = Resistor [tolerance=±5% resistance=220 package=THT]
  R5 = Resistor [tolerance=±5% resistance=220 package=THT]
  R6 = Resistor [tolerance=±5% resistance=220 package=THT]
  LED4 = LED - 5mm [color="Red (633nm)" package="5 mm [THT]"]
  LED5 = LED - 5mm [color="Yellow (595nm)" package="5 mm [THT]"]
  LED6 = LED - 5mm [color="Green (565nm)" package="5 mm [THT]"]
  J1 = Piezo Speaker
  S1 = Pushbutton [package=THT]
  R7 = Resistor [tolerance=±5% resistance=100k package=THT]

nets:
  N1: Bauteil1.D8, S1.leg0, R7.Pin_1
  N2: Bauteil1.D11_PWM/MOSI, LED3.anode
  N3: Bauteil1.D12/MISO, LED2.anode
  N4: Bauteil1.D13/SCK, LED1.anode
  N5: Bauteil1.D3_PWM, J1.pin2
  N6: Bauteil1.D4, LED4.anode
  N7: Bauteil1.D5_PWM, LED5.anode
  N8: Bauteil1.D6_PWM, LED6.anode
  N9: Bauteil1.5V, S1.leg1
  N10: Bauteil1.GND, R1.Pin_1, R2.Pin_1, R3.Pin_1, R4.Pin_1, R5.Pin_1, R6.Pin_1, J1.pin1, R7.Pin_0
  N11: R1.Pin_0, LED1.cathode
  N12: R2.Pin_0, LED2.cathode
  N13: R3.Pin_0, LED3.cathode
  N14: R4.Pin_0, LED4.cathode
  N15: R5.Pin_0, LED5.cathode
  N16: R6.Pin_0, LED6.cathode
